// Logisim project Project1.circ as structural Verilog: 5 circuits, main circuit main
module main (
);

  wire clock_1_out, clock_2_out, decimal_counter_1_l0, decimal_counter_1_l1, decimal_counter_1_l2,
       decimal_counter_1_l3, hex_logic_1_a, hex_logic_1_b, hex_logic_1_c, hex_logic_1_d, hex_logic_1_e,
       hex_logic_1_f, hex_logic_1_g, hexadecimal_counter_1_l0, hexadecimal_counter_1_l1,
       hexadecimal_counter_1_l2, hexadecimal_counter_1_l3, logic_1_a, logic_1_b, logic_1_c, logic_1_d,
       logic_1_e, logic_1_f, logic_1_g;

  Clock clock_1 (.out(clock_1_out));
  Clock clock_2 (.out(clock_2_out));
  hexadecimal_counter hexadecimal_counter_1 (
    .Clock(clock_1_out), .L0(hexadecimal_counter_1_l0), .L1(hexadecimal_counter_1_l1),
    .L2(hexadecimal_counter_1_l2), .L3(hexadecimal_counter_1_l3));  // open: IS_FIFTEEN
  hex_logic hex_logic_1 (
    .a(hex_logic_1_a), .b(hex_logic_1_b), .c(hex_logic_1_c), .d(hex_logic_1_d), .e(hex_logic_1_e),
    .f(hex_logic_1_f), .g(hex_logic_1_g), .w(hexadecimal_counter_1_l0), .x(hexadecimal_counter_1_l1),
    .y(hexadecimal_counter_1_l2), .z(hexadecimal_counter_1_l3));
  decimal_counter decimal_counter_1 (
    .Clock(clock_2_out), .L0(decimal_counter_1_l0), .L1(decimal_counter_1_l1), .L2(decimal_counter_1_l2),
    .L3(decimal_counter_1_l3));  // open: IS_NINE
  \logic  logic_1 (
    .a(logic_1_a), .b(logic_1_b), .c(logic_1_c), .d(logic_1_d), .e(logic_1_e), .f(logic_1_f), .g(logic_1_g),
    .w(decimal_counter_1_l0), .x(decimal_counter_1_l1), .y(decimal_counter_1_l2), .z(decimal_counter_1_l3));
  _7_Segment_Display u_7_segment_display_1 (
    .g(hex_logic_1_g), .f(hex_logic_1_f), .a(hex_logic_1_a), .b(hex_logic_1_b), .e(hex_logic_1_e),
    .d(hex_logic_1_d), .c(hex_logic_1_c));  // open: dp
  _7_Segment_Display u_7_segment_display_2 (
    .g(logic_1_g), .f(logic_1_f), .a(logic_1_a), .b(logic_1_b), .e(logic_1_e), .d(logic_1_d), .c(logic_1_c));  // open: dp
endmodule

module \logic  (
  input  z,
  input  y,
  input  x,
  input  w,
  output a,
  output b,
  output c,
  output d,
  output e,
  output f,
  output g
);

  wire and_1_out, and_2_out, and_3_out, and_4_out, nand_1_out, nand_2_out, nand_3_out, nor_1_out, not_1_out,
       not_2_out, not_3_out, not_4_out, not_5_out, or_1_out, or_2_out, or_3_out, or_4_out, xnor_1_out,
       xor_1_out;

  and and_1 (and_1_out, y, w);
  nand nand_1 (nand_1_out, x, w);
  not not_1 (not_1_out, z);
  nand nand_2 (nand_2_out, y, w);
  or or_1 (or_1_out, y, w);
  not not_2 (not_2_out, x);
  nand nand_3 (nand_3_out, x, w);
  or or_2 (or_2_out, x, w);
  not not_3 (not_3_out, x);
  or or_3 (or_3_out, x, w, y);
  or or_4 (or_4_out, z, xnor_1_out);
  xnor xnor_1 (xnor_1_out, x, and_1_out);
  and and_2 (and_2_out, y, not_4_out);
  not not_4 (not_4_out, x);
  and and_3 (and_3_out, y, nand_1_out);
  nor nor_1 (nor_1_out, w, x);
  not not_5 (not_5_out, w);
  and and_4 (and_4_out, not_5_out, x);
  xor xor_1 (xor_1_out, x, y);
  nand nand_4 (a, not_1_out, nand_2_out, or_1_out, not_2_out);
  nand nand_5 (b, y, nand_3_out, or_2_out);
  or or_5 (c, y, not_3_out, w);
  nand nand_6 (d, or_3_out, or_4_out);
  nor nor_2 (e, w, and_2_out);
  or or_6 (f, z, and_3_out, nor_1_out);
  or or_7 (g, z, and_4_out, xor_1_out);
endmodule

module hex_logic (
  input  z,
  input  y,
  input  x,
  input  w,
  output a,
  output b,
  output c,
  output d,
  output e,
  output f,
  output g
);

  wire and_1_out, and_2_out, and_3_out, and_4_out, and_5_out, and_6_out, and_7_out, and_8_out, and_9_out,
       and_10_out, and_11_out, and_12_out, and_13_out, and_14_out, and_15_out, and_16_out, and_17_out,
       and_18_out, and_19_out, and_20_out, and_21_out, and_22_out, and_23_out, and_24_out, and_25_out,
       and_26_out, and_27_out, and_28_out, and_29_out, and_30_out, and_31_out, and_32_out, and_33_out,
       and_34_out, and_35_out, not_1_out, not_2_out, not_3_out, not_4_out;

  not not_1 (not_1_out, z);
  not not_2 (not_2_out, y);
  not not_3 (not_3_out, x);
  not not_4 (not_4_out, w);
  and and_1 (and_1_out, not_2_out, not_4_out);
  and and_2 (and_2_out, not_1_out, x);
  and and_3 (and_3_out, y, x);
  and and_4 (and_4_out, z, not_4_out);
  and and_5 (and_5_out, not_1_out, y, w);
  and and_6 (and_6_out, z, not_2_out, not_3_out);
  and and_7 (and_7_out, not_1_out, not_2_out);
  and and_8 (and_8_out, not_2_out, not_4_out);
  and and_9 (and_9_out, not_1_out, not_3_out, not_4_out);
  and and_10 (and_10_out, not_1_out, x, w);
  and and_11 (and_11_out, z, not_3_out, w);
  and and_12 (and_12_out, not_1_out, not_3_out);
  and and_13 (and_13_out, not_1_out, w);
  and and_14 (and_14_out, not_1_out, y);
  and and_15 (and_15_out, not_3_out, w);
  and and_16 (and_16_out, z, not_2_out);
  and and_17 (and_17_out, z, not_3_out);
  and and_18 (and_18_out, not_1_out, not_2_out, not_4_out);
  and and_19 (and_19_out, not_2_out, x, w);
  and and_20 (and_20_out, y, not_3_out, w);
  and and_21 (and_21_out, y, x, not_4_out);
  and and_22 (and_22_out, z, y);
  and and_23 (and_23_out, z, x);
  and and_24 (and_24_out, not_2_out, not_4_out);
  and and_25 (and_25_out, x, not_4_out);
  and and_26 (and_26_out, z, not_2_out);
  and and_27 (and_27_out, z, x);
  and and_28 (and_28_out, y, not_4_out);
  and and_29 (and_29_out, not_3_out, not_4_out);
  and and_30 (and_30_out, not_1_out, y, not_3_out);
  and and_31 (and_31_out, z, w);
  and and_32 (and_32_out, z, not_2_out);
  and and_33 (and_33_out, not_2_out, x);
  and and_34 (and_34_out, x, not_4_out);
  and and_35 (and_35_out, not_1_out, y, not_3_out);
  or or_1 (a, and_1_out, and_2_out, and_3_out, and_4_out, and_5_out, and_6_out);
  or or_2 (b, and_7_out, and_8_out, and_9_out, and_10_out, and_11_out);
  or or_3 (c, and_12_out, and_13_out, and_14_out, and_15_out, and_16_out);
  or or_4 (d, and_17_out, and_18_out, and_19_out, and_20_out, and_21_out);
  or or_5 (e, and_22_out, and_23_out, and_24_out, and_25_out);
  or or_6 (f, and_26_out, and_27_out, and_28_out, and_29_out, and_30_out);
  or or_7 (g, and_31_out, and_32_out, and_33_out, and_34_out, and_35_out);
endmodule

module decimal_counter (
  input  Clock,
  output L0,
  output L1,
  output L2,
  output L3,
  output IS_NINE
);

  wire and_2_out, and_3_out, and_4_out, and_5_out, and_6_out, and_7_out, and_8_out, D1_qn, D2_qn, D3_qn,
       D4_qn, or_1_out, or_2_out, or_3_out;

  and and_1 (IS_NINE, L3, D2_qn, D3_qn, L0);
  and and_2 (and_2_out, L3, D4_qn);
  and and_3 (and_3_out, L2, L1, L0);
  and and_4 (and_4_out, L2, D3_qn);
  and and_5 (and_5_out, L2, D4_qn);
  and and_6 (and_6_out, D2_qn, L1, L0);
  and and_7 (and_7_out, L1, D4_qn);
  and and_8 (and_8_out, D1_qn, D3_qn, L0);
  or or_1 (or_1_out, and_2_out, and_3_out);
  or or_2 (or_2_out, and_4_out, and_5_out, and_6_out);
  or or_3 (or_3_out, and_7_out, and_8_out);
  D_Flip_Flop #(.trigger("falling")) D1 (.clk(Clock), .D(or_1_out), .Q(L3), .Qn(D1_qn));  // open: preset, en, reset
  D_Flip_Flop #(.trigger("falling")) D2 (.clk(Clock), .D(or_2_out), .Q(L2), .Qn(D2_qn));  // open: preset, en, reset
  D_Flip_Flop #(.trigger("falling")) D3 (.clk(Clock), .D(or_3_out), .Q(L1), .Qn(D3_qn));  // open: preset, en, reset
  D_Flip_Flop #(.trigger("falling")) D4 (.clk(Clock), .D(D4_qn), .Q(L0), .Qn(D4_qn));  // open: preset, en, reset
endmodule

module hexadecimal_counter (
  input  Clock,
  output L0,
  output L1,
  output L2,
  output L3,
  output IS_FIFTEEN
);

  wire and_2_out, and_3_out, and_4_out, and_5_out, and_6_out, and_7_out, and_8_out, and_9_out, and_10_out,
       D1_qn, D2_qn, D3_qn, D4_qn, or_1_out, or_2_out, or_3_out;

  and and_1 (IS_FIFTEEN, L3, L2, L1, L0);
  and and_2 (and_2_out, L3, D2_qn);
  and and_3 (and_3_out, L3, D3_qn);
  and and_4 (and_4_out, L3, D4_qn);
  and and_5 (and_5_out, D1_qn, L2, L1, L0);
  and and_6 (and_6_out, L2, D3_qn);
  and and_7 (and_7_out, L2, D4_qn);
  and and_8 (and_8_out, D2_qn, L1, L0);
  and and_9 (and_9_out, L1, D4_qn);
  and and_10 (and_10_out, D3_qn, L0);
  or or_1 (or_1_out, and_2_out, and_3_out, and_4_out, and_5_out);
  or or_2 (or_2_out, and_6_out, and_7_out, and_8_out);
  or or_3 (or_3_out, and_9_out, and_10_out);
  D_Flip_Flop #(.trigger("falling")) D1 (.clk(Clock), .D(or_1_out), .Q(L3), .Qn(D1_qn));  // open: preset, en, reset
  D_Flip_Flop #(.trigger("falling")) D2 (.clk(Clock), .D(or_2_out), .Q(L2), .Qn(D2_qn));  // open: preset, en, reset
  D_Flip_Flop #(.trigger("falling")) D3 (.clk(Clock), .D(or_3_out), .Q(L1), .Qn(D3_qn));  // open: preset, en, reset
  D_Flip_Flop #(.trigger("falling")) D4 (.clk(Clock), .D(D4_qn), .Q(L0), .Qn(D4_qn));  // open: preset, en, reset
endmodule
